# Fritzing sketch R04_N1 sem temperatura (saved by Fritzing 0.9.6b)
breadboards: 1

parts:
  Componente1 = Arduino Uno (Rev3)
  1 = pH_4502c module [package="SIP (Single Inline) [THT]"]

nets:
  N1: Componente1.A0, 1.PO
  5V: Componente1.5V, 1.VCC
  GND: Componente1.GND, 1.GND

custom parts:
  pH_4502c module: ph
