# Fritzing sketch R04_N1 (saved by Fritzing 0.9.6b)
breadboards: 1

parts:
  Componente1 = Arduino Uno (Rev3)
  1 = pH_4502c module [package="SIP (Single Inline) [THT]"]
  R1 = Resistor [tolerance=±5% resistance=4.7k power=0.25 package=THT]
  DS2 = DS18B20 adaptado

nets:
  N1: Componente1.A0, 1.PO
  N2: Componente1.D2, R1.Pin_0, DS2.DQ
  5V: Componente1.5V, 1.VCC, R1.Pin_1, DS2.VDD
  GND: Componente1.GND, 1.GND, DS2.GND

custom parts:
  pH_4502c module: ph
