# Fritzing sketch R04_N2 (saved by Fritzing 0.9.6b)
breadboards: 1

parts:
  Componente1 = Arduino Uno (Rev3)
  1 = pH_4502c module [package="SIP (Single Inline) [THT]"]
  R1 = Resistor [tolerance=±5% resistance=4.7k power=0.25 package=THT]
  DS2 = DS18B20 adaptado
  LCM1602_IIC2 = LCM1602 IIC [part_number="LCM1602 IIC" chip_label="LCM1602 IIC" package="DIP (Dual Inline) [THT]"]
  LCD2 = LCD screen

nets:
  N1: Componente1.A0, 1.PO
  N2: Componente1.A4/SDA, LCM1602_IIC2.SDA
  N3: Componente1.A5/SCL, LCM1602_IIC2.SCL
  N4: Componente1.D2, R1.Pin_0, DS2.DQ
  VCC: Componente1.5V, 1.VCC, R1.Pin_1, DS2.VDD, LCM1602_IIC2.VCC
  GND: Componente1.GND, 1.GND, DS2.GND, LCM1602_IIC2.GND
  VSS: LCM1602_IIC2.VSS, LCD2.VSS
  VDD: LCM1602_IIC2.VDD, LCD2.VDD
  N5: LCM1602_IIC2.V0, LCD2.V0
  N6: LCM1602_IIC2.RS, LCD2.RS
  N7: LCM1602_IIC2.RW, LCD2.R/W
  N8: LCM1602_IIC2.E, LCD2.E
  N9: LCM1602_IIC2.D0, LCD2.DB0
  N10: LCM1602_IIC2.D1, LCD2.DB1
  N11: LCM1602_IIC2.D2, LCD2.DB2
  N12: LCM1602_IIC2.D3, LCD2.DB3
  N13: LCM1602_IIC2.D4, LCD2.DB4
  N14: LCM1602_IIC2.D5, LCD2.DB5
  N15: LCM1602_IIC2.D6, LCD2.DB6
  N16: LCM1602_IIC2.D7, LCD2.DB7
  N17: LCM1602_IIC2.A, LCD2.LED+
  N18: LCM1602_IIC2.K, LCD2.LED-
  N19: LCM1602_IIC2.LED_A, LCM1602_IIC2.LED_B

custom parts:
  pH_4502c module: ph
  LCM1602 IIC: I2C-Module to use a 1602 or 2004 LCD on with the wire.h libory Serial LCD Modul
